# Fritzing sketch Schematic (saved by Fritzing 0.9.9b)
circuit board: 8.46667cm x 5.64444cm
breadboards: 2

parts:
  R1 = Resistor [tolerance=±5% power=0.25 resistance=10k package=THT]
  R2 = Resistor [tolerance=±5% power=0.25 resistance=10k package=THT]
  R3 = Resistor [tolerance=±5% power=0.25 resistance=10k package=THT]
  S2 = SWITCH-MOMENTARY-2 [package=tactile-switch-1101ne]
  S3 = SWITCH-MOMENTARY-2 [package=tactile-switch-1101ne]
  J1 = Piezo Speaker
  Part2 = Bluetooth HC-05 Macho
  R4 = Resistor [tolerance=±5% resistance=1k power=0.25 package=THT]
  R5 = Resistor [tolerance=±5% power=0.25 resistance=2.0k package=THT]
  LCD1 = LCD screen
  R6 = Resistor [tolerance=±5% power=0.25 resistance=240 package=THT]
  V1 = DC Power [voltage=5V]
  P1 = Rotary Potentiometer (Small) [maximum_resistance=10kΩ package=THT]
  Y1 = CRYSTAL [package=hc49u-v]
  C1 = Ceramic Capacitor [capacitance=22pF voltage=20V package="0805 [SMD, multilayer]"]
  C2 = Ceramic Capacitor [capacitance=22pF voltage=20V package="0805 [SMD, multilayer]"]
  R7 = Resistor [tolerance=±5% resistance=10k power=0.25 package=THT]
  S4 = SWITCH-MOMENTARY-2 [package=tactile-switch-1101ne]
  S1 = SWITCH-MOMENTARY-2 [package=tactile-switch-1101ne]
  LED1 = LED - 3mm [color="Red (633nm)" current=0.030 package="3 mm [THT]"]
  IC1 = atmega328 [package=dip]
  R8 = Resistor [tolerance=±5% power=0.25 resistance=240 package=THT]
  C3 = Ceramic Capacitor [capacitance=22pF voltage=20V package="0805 [SMD, multilayer]"]
  Part3 = FTDI Basic Programmer
  C4 = Ceramic Capacitor [capacitance=22pF voltage=20V package="0805 [SMD, multilayer]"]

nets:
  N1: R1.Pin_0, S1.1, IC1.D9_(PWM)
  GND: R1.Pin_1, R2.Pin_1, R3.Pin_1, J1.pin2, Part2.GND, R5.Pin_1, LCD1.R/W, LCD1.LED-, V1.V-, C1.0, C2.0, S4.1, LED1.cathode, IC1.GND, C3.1, Part3.GND
  N2: R2.Pin_0, S2.1, IC1.D10_(PWM)
  N3: R3.Pin_0, S3.1, IC1.D11_(PWM)
  VCC: S2.2, S3.2, Part2.VCC, LCD1.VDD, R6.Pin_0, V1.V+, P1.leg2, R7.Pin_0, S1.2, IC1.VCC, IC1.AVCC, C3.0, Part3.POWER
  N4: J1.pin1, IC1.D8
  N5: Part2.TXD, R4.Pin_1, R5.Pin_0
  N6: Part2.RXD, IC1.D12
  N7: R4.Pin_0, IC1.D13
  N8: LCD1.VSS, P1.leg1
  N9: LCD1.V0, P1.wiper
  N10: LCD1.RS, IC1.D2
  N11: LCD1.E, IC1.D3_(PWM)
  N12: LCD1.DB4, IC1.D4
  N13: LCD1.DB5, IC1.D5_(PWM)
  N14: LCD1.DB6, IC1.D6_(PWM)
  N15: LCD1.DB7, IC1.D7
  N16: LCD1.LED+, R6.Pin_1
  N17: Y1.1, C1.1, IC1.XLAT1
  N18: Y1.2, C2.1, IC1.XLAT2
  N19: R7.Pin_1, S4.2, IC1.RESET, C4.0
  N20: LED1.anode, R8.Pin_0
  N21: IC1.D0_(RX), Part3.TXO
  N22: IC1.D1_(TX), Part3.RXI
  N23: Part3.DTR, C4.1
